# Fritzing sketch enc28j60 (saved by Fritzing 0.9.2b)
circuit board: 6.08948cm x 6.81842cm
breadboards: 1

parts:
  Arduino = Arduino Nano (Rev3.0)
  Sensor = female alternating pin header, 3 pins [form="♀ (female)"]
  Fonte = male pin header, 2 pins [form="♂ (male)"]
  Enc28j60 = ENC28J60 Breakout Board

nets:
  GND: Arduino.GND, Sensor.pin1, Fonte.pin1, Enc28j60.GND
  N1: Arduino.D2, Enc28j60.INT
  N2: Arduino.D3, Sensor.pin2
  N3: Arduino.D10, Enc28j60.CS
  N4: Arduino.D11/MOSI, Enc28j60.SI
  N5: Arduino.D12/MISO, Enc28j60.SO
  N6: Arduino.VIN, Fonte.pin2
  5V: Arduino.5V, Sensor.pin3, Enc28j60.VCC
  N7: Arduino.D13/SCK, Enc28j60.SCK

custom parts:
  ENC28J60 Breakout Board: This is a breakout board for the Microchip ENC28J60 stand-alone ethernet controller. The ENC28J60 has an SPI interface. It operates at 3.3 Volts.
