# Fritzing sketch schematic (saved by Fritzing 0.9.2b)
circuit board: 5.8cm x 3.2cm
breadboards: 1

parts:
  C2 = Electrolytic Capacitor [capacitance=10µF part_number=3 package="100 mil [THT, electrolytic]"]
  C1 = Electrolytic Capacitor [part_number=1 package="100 mil [THT, electrolytic]"]
  J2 = shrouded pin header, 8 pins [form="♂ (shrouded male)"]
  R2 = Resistor [tolerance=±5% resistance=240 part_number=5 package=THT]
  U1 = Voltage Regulator [part_number=2 package=to220-adj]
  Power_plug1 = Power plug
  J5 = male pin header, 3 pins [form="♂ (male)"]
  J1 = female pin header, 5 pins [form="♀ (female)" part_number=6]
  J4 = male pin header, 3 pins [form="♂ (male)"]
  R1 = Resistor [tolerance=±5% resistance=390 part_number=4 package=THT]

nets:
  N1: C2.-, C1.-, J2.pin4, Power_plug1.VCC, J5.pin3, J1.pin3, R1.Pin_1
  N2: C2.+, J2.pin6, J2.pin8, R2.Pin_0, U1.IN, J4.pin1
  N3: C1.+, U1.OUT, Power_plug1.GND, J5.pin1
  N4: J2.pin1, J1.pin5
  N5: J2.pin2, J4.pin2
  N6: J2.pin5, J1.pin4
  N7: R2.Pin_1, U1.ADJ, R1.Pin_0
  N8: J5.pin2, J4.pin3

custom parts:
  Electrolytic Capacitor: A small electrolytic capacitor
